# Fritzing sketch Схема подключения (saved by Fritzing 0.9.3b)
circuit board: 8.46667cm x 5.64444cm

parts:
  Часть1 = Soil Moisture Sensor
  Часть2 = Arduino Nano (Rev3.0)
  Часть3 = Soil Moisture Sensor
  Часть4 = Soil Moisture Sensor
  Часть5 = Soil Moisture Sensor
  Часть6 = Soil Moisture Sensor
  U1 = 74HC595 [package="DIP16 [THT]"]
  RHT1 = Humidity and Temperature Sensor RHT03
  U2 = 74HC595 [package="DIP16 [THT]"]
  DS1 = DS18B20 1-Wire Temperature Sensor [part_number=DS18B20]
  DS2 = DS18B20 1-Wire Temperature Sensor [part_number=DS18B20]
  DS3 = DS18B20 1-Wire Temperature Sensor [part_number=DS18B20]
  DS4 = DS18B20 1-Wire Temperature Sensor [part_number=DS18B20]
  DS5 = DS18B20 1-Wire Temperature Sensor [part_number=DS18B20]

nets:
  N1: Часть1.SIG, U1.OE
  GND: Часть1.GND, Часть2.GND, Часть3.GND, Часть4.GND, Часть5.GND, Часть6.GND, U1.GND, RHT1.GND_1, RHT1.GND_2, DS1.GND, DS2.GND, DS3.GND, DS4.GND, DS5.GND
  VCC: Часть1.VCC, Часть2.5V, Часть3.VCC, Часть4.VCC, Часть5.VCC, Часть6.VCC, U1.VCC, RHT1.Vcc, DS1.VDD, DS2.VDD, DS3.VDD, DS4.VDD, DS5.VDD
  N2: Часть2.D5, U1.Q2
  N3: Часть2.D6, RHT1.Data-signal
  N4: Часть2.D7, U2.Q2
  N5: Часть3.SIG, U1.ST_CP
  N6: Часть4.SIG, U1.DS
  N7: Часть5.SIG, U1.SH_CP
  N8: Часть6.SIG, U1.Q3
  N9: U2.Q3, DS5.DQ
  N10: U2.SH_CP, DS4.DQ
  N11: U2.ST_CP, DS3.DQ
  N12: U2.OE, DS2.DQ
  N13: U2.DS, DS1.DQ
